// Digital circuit system.dig as structural Verilog
module system (
  input  clock
);

  wire and_1_out, and_2_out, not_1_out, not_2_out, not_3_out;
  wire [3:0] MI_d_2, MI_d_3, MI_d_4, MI_d_5;
  wire [9:0] CONTROLE_d;
  wire [15:0] MI_d;
  wire [23:0] PC_q;
  wire [31:0] add_1_s, add_2_s, bitextender_1_out, DADOS_d, multiplexer_1_out, multiplexer_2_out, regs_1_p4,
       regs_1_p7, regs_1_p8, ula_32bits_1_r;
  wire [31:24] PC_q_2;

  D_FF #(.Bits(32)) PC (.D(multiplexer_1_out), .C(clock), .Q({PC_q_2, PC_q}));  // open: nQ
  Add #(.Bits(32)) add_1 (.a(32'h1), .b({PC_q_2, PC_q}), .c_i(1'b0), .s(add_1_s));  // open: c_o
  ROM #(.AddrBits(24), .isProgramMemory("true"), .Bits(32)) MI (
    .A(PC_q), .sel(1'b1), .D({MI_d_5, MI_d_4, MI_d_3, MI_d_2, MI_d}));
  Multiplexer #(.Selector_Bits(2), .Bits(32)) multiplexer_1 (
    .sel(CONTROLE_d[1:0]), .in_0(add_1_s), .in_1(add_2_s), .in_2(ula_32bits_1_r), .in_3({32{1'b0}}),
    .out(multiplexer_1_out));
  Add #(.Bits(32)) add_2 (.a({PC_q_2, PC_q}), .b(bitextender_1_out), .c_i(1'b0), .s(add_2_s));  // open: c_o
  ROM #(.AddrBits(4), .Bits(10)) CONTROLE (.A(MI_d_5), .sel(1'b1), .D(CONTROLE_d));
  BitExtender #(.inputBits(16), .outputBits(32)) bitextender_1 (.in(MI_d), .out(bitextender_1_out));
  // regs regs_1: pin names not known; wires that end beside it: MI_d_4, MI_d_3, MI_d_2, regs_1_p4, CONTROLE_d[3], clock, regs_1_p7, regs_1_p8
  Multiplexer #(.Bits(32)) multiplexer_2 (
    .sel(CONTROLE_d[6]), .in_0(regs_1_p8), .in_1(bitextender_1_out), .out(multiplexer_2_out));
  ula_32bits ula_32bits_1 (
    .R(ula_32bits_1_r), .F(CONTROLE_d[9:7]), .A(regs_1_p7), .B(multiplexer_2_out));  // open: overflow, zero, neg
  Multiplexer #(.Selector_Bits(2), .Bits(32)) multiplexer_3 (
    .sel(CONTROLE_d[5:4]), .in_0(ula_32bits_1_r), .in_1(DADOS_d), .in_2(add_1_s), .in_3({32{1'b0}}),
    .out(regs_1_p4));
  RAMDualPort #(.AddrBits(24), .Bits(32)) DADOS (
    .A(ula_32bits_1_r[23:0]), .Din(regs_1_p8), .str(and_1_out), .C(clock), .ld(not_3_out), .D(DADOS_d));
  and and_1 (and_1_out, not_3_out, CONTROLE_d[2]);
  not not_1 (not_1_out, MI_d_5[2]);
  not not_2 (not_2_out, MI_d_5[0]);
  not not_3 (not_3_out, and_2_out);
  and and_2 (and_2_out, ula_32bits_1_r[24], ula_32bits_1_r[25], ula_32bits_1_r[26], ula_32bits_1_r[27], ula_32bits_1_r[28], ula_32bits_1_r[29], ula_32bits_1_r[30], ula_32bits_1_r[31], not_2_out, MI_d_5[1], not_1_out, MI_d_5[3]);
  Terminal #(.termWidth(80), .termHeight(24)) TERMINAL (.D(regs_1_p8), .C(clock), .en(and_2_out));

  // Notes on the sheet:
  //   PC + 1
  //   contents of MI (hex, n*v repeats v):
  //   800b0041,800a0009,80090000,80080003,80050000,8001ffff,8002fffe
  //   ,ea090001,a1b00000,59850000,a2500000
  //   CONTROLE
  //   contents of CONTROLE (hex, n*v repeats v):
  //   8,88,108,188,208,288,308,388,48,58,44,0,0,29
  //   wrReg
  //   selB
  //   selC
  //   aluFunc
  //   ULA
  //   MD
  //   wrMem
  //   TERMINAL
endmodule
